# Fritzing sketch temperatura (saved by Fritzing 0.9.3b)
breadboards: 1

parts:
  R1 = Resistor [tolerance=±5% resistance=220 package=THT]
  Grove1 = Grove OLED 128x96
  Part1 = Arduino Uno (Rev3)
  R2 = Temperature Sensor (Thermistor) [thermistor_type=NTC package=THT]

nets:
  VCC: R1.Pin_0, Grove1.VCC, Part1.A0, Part1.5V, R2.pin_0, R2.pin_1
  GND: R1.Pin_1, Grove1.GND, Part1.GND
  N1: Grove1.SDA, Part1.A5/SCL
  N2: Grove1.SCL, Part1.A4/SDA
